// Logisim project PROCESSOR.circ as structural Verilog
module main (
  input  A,
  input  B,
  input  C,
  output out_4,
  output out_5,
  output out_6,
  output out_7,
  output out_8,
  output out_9,
  output out_10
);

  wire not_1_out, not_2_out, not_3_out, not_4_out, not_5_out, not_6_out, not_7_out, not_8_out, not_9_out;

  not not_1 (not_1_out, A);
  not not_2 (not_2_out, B);
  not not_3 (not_3_out, A);
  not not_4 (not_4_out, C);
  not not_5 (not_5_out, A);
  not not_6 (not_6_out, B);
  not not_7 (not_7_out, C);
  not not_8 (not_8_out, B);
  not not_9 (not_9_out, C);
  and and_1 (out_4, not_1_out, not_2_out, C);
  and and_2 (out_5, not_3_out, B, not_4_out);
  and and_3 (out_6, not_5_out, B, C);
  and and_4 (out_7, A, not_6_out, not_7_out);
  and and_5 (out_8, A, not_8_out, C);
  and and_6 (out_9, A, B, not_9_out);
  and and_7 (out_10, A, B, C);
endmodule

module SUM (
  input  in_1,
  input  in_2,
  input  in_3,
  output out_4,
  output out_5
);

  wire and_1_out, and_2_out, and_3_out, xor_1_out;

  and and_1 (and_1_out, in_2, in_3);
  and and_2 (and_2_out, in_2, in_1);
  and and_3 (and_3_out, in_3, in_1);
  xor xor_1 (xor_1_out, in_2, in_3);
  xor xor_2 (out_4, in_1, xor_1_out);
  or or_1 (out_5, and_1_out, and_2_out, and_3_out);
endmodule

module SUB (
  input  in_1,
  input  in_2,
  input  in_3,
  output out_4,
  output out_5
);

  wire and_1_out, and_2_out, and_3_out, not_1_out, not_2_out, xor_1_out;

  not not_1 (not_1_out, in_1);
  not not_2 (not_2_out, in_1);
  xor xor_1 (xor_1_out, in_2, in_3);
  and and_1 (and_1_out, in_2, in_3);
  and and_2 (and_2_out, in_2, not_1_out);
  and and_3 (and_3_out, in_3, not_2_out);
  xor xor_2 (out_4, in_1, xor_1_out);
  or or_1 (out_5, and_1_out, and_2_out, and_3_out);
endmodule

module NOT (
  input  in_1,
  output out_2
);

  not not_1 (out_2, in_1);
endmodule

module AND (
  input  in_1,
  input  in_2,
  output out_3
);

  and and_1 (out_3, in_1, in_2);
endmodule

module OR (
  input  in_1,
  input  in_2,
  output out_3
);

  or or_1 (out_3, in_1, in_2);
endmodule

module NOR (
  input  in_1,
  input  in_2,
  output out_3
);

  nor nor_1 (out_3, in_1, in_2);
endmodule

module NAND (
  input  in_1,
  input  in_2,
  output out_3
);

  nand nand_1 (out_3, in_1, in_2);
endmodule

module EXIT_BIT (
  input  in_1,
  input  in_2,
  input  in_3,
  input  in_4,
  input  in_5,
  input  in_6,
  input  in_7,
  input  in_8,
  input  in_9,
  input  in_10,
  input  in_11,
  input  in_12,
  input  in_13,
  input  in_14,
  input  in_15,
  input  in_16,
  output out_17,
  output out_18
);

  wire and_1_out, and_2_out, and_3_out, and_4_out, and_5_out, and_6_out, and_7_out, and_8_out, and_9_out,
       or_1_out, or_2_out;

  and and_1 (and_1_out, in_1, in_2);
  and and_2 (and_2_out, in_3, in_4);
  and and_3 (and_3_out, in_5, in_6);
  and and_4 (and_4_out, in_7, in_8);
  and and_5 (and_5_out, in_9, in_10);
  and and_6 (and_6_out, in_11, in_12);
  and and_7 (and_7_out, in_13, in_14);
  or or_1 (or_1_out, and_1_out, and_2_out, and_3_out, and_4_out, and_5_out);
  or or_2 (or_2_out, and_6_out, and_7_out);
  and and_8 (and_8_out, and_6_out, in_15);
  and and_9 (and_9_out, and_7_out, in_16);
  or or_3 (out_17, or_1_out, or_2_out);
  or or_4 (out_18, and_8_out, and_9_out);
endmodule

module SUM_1_BIT (
  input  in_1,
  input  in_2,
  output out_3,
  output out_4
);

  xor xor_1 (out_3, in_1, in_2);
  and and_1 (out_4, in_2, in_1);
endmodule

module SUB_1_bit (
  input  in_1,
  input  in_2,
  output out_3,
  output out_4
);

  wire not_1_out;

  not not_1 (not_1_out, in_1);
  and and_1 (out_4, in_2, not_1_out);
  xor xor_1 (out_3, in_1, in_2);
endmodule

module ULA (
  input  in_1,
  input  in_2,
  input  in_3,
  input  in_4,
  input  in_5,
  input  in_6,
  input  in_7,
  input  in_8,
  input  in_9,
  input  in_10,
  input  in_11,
  input  in_12,
  input  in_13,
  input  in_14,
  input  in_15,
  input  in_16,
  input  in_17,
  input  in_18,
  input  in_19,
  output out_20,
  output out_21,
  output out_22,
  output out_23,
  output out_24,
  output out_25,
  output out_26,
  output out_27,
  output OVERFLOW
);

  wire main_1_out_4, main_1_out_5, main_1_out_6, main_1_out_7, main_1_out_8, main_1_out_9, main_1_out_10,
       ula_1_bit_1_out_12, ula_1_bit_2_out_12, ula_1_bit_3_out_12, ula_1_bit_4_out_12, ula_1_bit_5_out_12,
       ula_1_bit_6_out_12, ula_1_n_cin_1_out_11;

  main main_1 (
    .A(in_17), .B(in_18), .C(in_19), .out_4(main_1_out_4), .out_5(main_1_out_5), .out_6(main_1_out_6),
    .out_7(main_1_out_7), .out_8(main_1_out_8), .out_9(main_1_out_9), .out_10(main_1_out_10));
  ULA_1_N_CIN ula_1_n_cin_1 (
    .A(in_1), .B(in_9), .in_3(main_1_out_4), .in_4(main_1_out_5), .in_5(main_1_out_6), .in_6(main_1_out_7),
    .in_7(main_1_out_8), .in_8(main_1_out_9), .in_9(main_1_out_10), .out_10(out_20),
    .out_11(ula_1_n_cin_1_out_11));
  ULA_1_BIT ula_1_bit_1 (
    .A(in_2), .B(in_10), .Ci_n(ula_1_n_cin_1_out_11), .in_4(main_1_out_4), .in_5(main_1_out_5),
    .in_6(main_1_out_6), .in_7(main_1_out_7), .in_8(main_1_out_8), .in_9(main_1_out_9),
    .in_10(main_1_out_10), .out_11(out_21), .out_12(ula_1_bit_1_out_12));
  ULA_1_BIT ula_1_bit_2 (
    .A(in_3), .B(in_11), .Ci_n(ula_1_bit_1_out_12), .in_4(main_1_out_4), .in_5(main_1_out_5),
    .in_6(main_1_out_6), .in_7(main_1_out_7), .in_8(main_1_out_8), .in_9(main_1_out_9),
    .in_10(main_1_out_10), .out_11(out_22), .out_12(ula_1_bit_2_out_12));
  ULA_1_BIT ula_1_bit_3 (
    .A(in_4), .B(in_12), .Ci_n(ula_1_bit_2_out_12), .in_4(main_1_out_4), .in_5(main_1_out_5),
    .in_6(main_1_out_6), .in_7(main_1_out_7), .in_8(main_1_out_8), .in_9(main_1_out_9),
    .in_10(main_1_out_10), .out_11(out_23), .out_12(ula_1_bit_3_out_12));
  ULA_1_BIT ula_1_bit_4 (
    .A(in_5), .B(in_13), .Ci_n(ula_1_bit_3_out_12), .in_4(main_1_out_4), .in_5(main_1_out_5),
    .in_6(main_1_out_6), .in_7(main_1_out_7), .in_8(main_1_out_8), .in_9(main_1_out_9),
    .in_10(main_1_out_10), .out_11(out_24), .out_12(ula_1_bit_4_out_12));
  ULA_1_BIT ula_1_bit_5 (
    .A(in_6), .B(in_14), .Ci_n(ula_1_bit_4_out_12), .in_4(main_1_out_4), .in_5(main_1_out_5),
    .in_6(main_1_out_6), .in_7(main_1_out_7), .in_8(main_1_out_8), .in_9(main_1_out_9),
    .in_10(main_1_out_10), .out_11(out_25), .out_12(ula_1_bit_5_out_12));
  ULA_1_BIT ula_1_bit_6 (
    .A(in_7), .B(in_15), .Ci_n(ula_1_bit_5_out_12), .in_4(main_1_out_4), .in_5(main_1_out_5),
    .in_6(main_1_out_6), .in_7(main_1_out_7), .in_8(main_1_out_8), .in_9(main_1_out_9),
    .in_10(main_1_out_10), .out_11(out_26), .out_12(ula_1_bit_6_out_12));
  ULA_1_BIT ula_1_bit_7 (
    .A(in_8), .B(in_16), .Ci_n(ula_1_bit_6_out_12), .in_4(main_1_out_4), .in_5(main_1_out_5),
    .in_6(main_1_out_6), .in_7(main_1_out_7), .in_8(main_1_out_8), .in_9(main_1_out_9),
    .in_10(main_1_out_10), .out_11(out_27), .out_12(OVERFLOW));
endmodule

module ULA_1_BIT (
  input  A,
  input  B,
  input  Ci_n,
  input  in_4,
  input  in_5,
  input  in_6,
  input  in_7,
  input  in_8,
  input  in_9,
  input  in_10,
  output out_11,
  output out_12
);

  wire and_1_out_3, and_2_out, and_3_out, and_4_out, and_5_out, and_6_out, and_7_out, and_8_out, and_9_out,
       and_10_out, nand_1_out_3, nor_1_out_3, not_1_out_2, or_1_out_3, or_2_out, or_3_out, sub_1_out_4,
       sub_1_out_5, sum_1_out_4, sum_1_out_5;

  NOT not_1 (.in_1(A), .out_2(not_1_out_2));
  AND and_1 (.in_1(A), .in_2(B), .out_3(and_1_out_3));
  OR or_1 (.in_1(A), .in_2(B), .out_3(or_1_out_3));
  NOR nor_1 (.in_1(A), .in_2(B), .out_3(nor_1_out_3));
  NAND nand_1 (.in_1(A), .in_2(B), .out_3(nand_1_out_3));
  SUM sum_1 (.in_1(A), .in_2(B), .in_3(Ci_n), .out_4(sum_1_out_4), .out_5(sum_1_out_5));
  SUB sub_1 (.in_1(A), .in_2(B), .in_3(Ci_n), .out_4(sub_1_out_4), .out_5(sub_1_out_5));
  and and_2 (and_2_out, not_1_out_2, in_4);
  and and_3 (and_3_out, and_1_out_3, in_5);
  and and_4 (and_4_out, or_1_out_3, in_6);
  and and_5 (and_5_out, nor_1_out_3, in_7);
  and and_6 (and_6_out, nand_1_out_3, in_8);
  and and_7 (and_7_out, sum_1_out_4, in_9);
  and and_8 (and_8_out, sub_1_out_4, in_10);
  and and_9 (and_9_out, sum_1_out_5, in_9);
  and and_10 (and_10_out, sub_1_out_5, in_10);
  or or_2 (or_2_out, and_2_out, and_3_out, and_4_out, and_5_out, and_6_out);
  or or_3 (or_3_out, and_7_out, and_8_out);
  or or_4 (out_12, and_9_out, and_10_out);
  or or_5 (out_11, or_2_out, or_3_out);
endmodule

module ULA_1_N_CIN (
  input  A,
  input  B,
  input  in_3,
  input  in_4,
  input  in_5,
  input  in_6,
  input  in_7,
  input  in_8,
  input  in_9,
  output out_10,
  output out_11
);

  wire and_1_out_3, and_2_out, and_3_out, and_4_out, and_5_out, and_6_out, and_7_out, and_8_out, and_9_out,
       and_10_out, nand_1_out_3, nor_1_out_3, not_1_out_2, or_1_out_3, or_2_out, or_3_out, sub_1_bit_1_out_3,
       sub_1_bit_1_out_4, sum_1_bit_1_out_3, sum_1_bit_1_out_4;

  NOT not_1 (.in_1(A), .out_2(not_1_out_2));
  AND and_1 (.in_1(A), .in_2(B), .out_3(and_1_out_3));
  OR or_1 (.in_1(A), .in_2(B), .out_3(or_1_out_3));
  NOR nor_1 (.in_1(A), .in_2(B), .out_3(nor_1_out_3));
  NAND nand_1 (.in_1(A), .in_2(B), .out_3(nand_1_out_3));
  SUM_1_BIT sum_1_bit_1 (.in_1(A), .in_2(B), .out_3(sum_1_bit_1_out_3), .out_4(sum_1_bit_1_out_4));
  SUB_1_bit sub_1_bit_1 (.in_1(A), .in_2(B), .out_3(sub_1_bit_1_out_3), .out_4(sub_1_bit_1_out_4));
  and and_2 (and_2_out, not_1_out_2, in_3);
  and and_3 (and_3_out, and_1_out_3, in_4);
  and and_4 (and_4_out, or_1_out_3, in_5);
  and and_5 (and_5_out, nor_1_out_3, in_6);
  and and_6 (and_6_out, nand_1_out_3, in_7);
  and and_7 (and_7_out, sum_1_bit_1_out_3, in_8);
  and and_8 (and_8_out, sub_1_bit_1_out_3, in_9);
  and and_9 (and_9_out, sum_1_bit_1_out_4, in_8);
  and and_10 (and_10_out, sub_1_bit_1_out_4, in_9);
  or or_2 (or_2_out, and_2_out, and_3_out, and_4_out, and_5_out, and_6_out);
  or or_3 (or_3_out, and_7_out, and_8_out);
  or or_4 (out_11, and_9_out, and_10_out);
  or or_5 (out_10, or_2_out, or_3_out);
endmodule

module PROCE (
  input  in_1,
  input  in_2,
  input  in_3,
  input  in_4,
  input  in_5,
  input  in_6,
  input  in_7,
  input  in_8,
  input  in_9,
  input  in_10,
  input  in_11,
  input  in_12,
  input  in_13,
  input  in_14,
  input  in_15,
  input  in_16,
  input  in_17,
  input  in_18,
  input  in_19,
  input  in_20,
  output out_21,
  output out_22,
  output out_23,
  output out_24,
  output out_25,
  output out_26,
  output out_27,
  output out_28,
  output out_29
);

  wire memory_8_bit_1_out_10, memory_8_bit_1_out_11, memory_8_bit_1_out_12, memory_8_bit_1_out_13,
       memory_8_bit_1_out_14, memory_8_bit_1_out_15, memory_8_bit_1_out_16, memory_8_bit_1_out_17,
       memory_8_bit_2_out_10, memory_8_bit_2_out_11, memory_8_bit_2_out_12, memory_8_bit_2_out_13,
       memory_8_bit_2_out_14, memory_8_bit_2_out_15, memory_8_bit_2_out_16, memory_8_bit_2_out_17,
       memory_8_bit_3_out_10, memory_8_bit_3_out_11, memory_8_bit_3_out_12;

  MEMORY_8_bit memory_8_bit_1 (
    .in_1(in_1), .in_2(in_2), .in_3(in_3), .in_4(in_4), .in_5(in_5), .in_6(in_6), .in_7(in_7), .in_8(in_8),
    .in_9(in_9), .out_10(memory_8_bit_1_out_10), .out_11(memory_8_bit_1_out_11),
    .out_12(memory_8_bit_1_out_12), .out_13(memory_8_bit_1_out_13), .out_14(memory_8_bit_1_out_14),
    .out_15(memory_8_bit_1_out_15), .out_16(memory_8_bit_1_out_16), .out_17(memory_8_bit_1_out_17));  // open: out_18
  MEMORY_8_bit memory_8_bit_2 (
    .in_1(in_10), .in_2(in_11), .in_3(in_12), .in_4(in_13), .in_5(in_14), .in_6(in_15), .in_7(in_16),
    .in_8(in_17), .in_9(in_9), .out_10(memory_8_bit_2_out_10), .out_11(memory_8_bit_2_out_11),
    .out_12(memory_8_bit_2_out_12), .out_13(memory_8_bit_2_out_13), .out_14(memory_8_bit_2_out_14),
    .out_15(memory_8_bit_2_out_15), .out_16(memory_8_bit_2_out_16), .out_17(memory_8_bit_2_out_17));  // open: out_18
  MEMORY_8_bit memory_8_bit_3 (
    .in_1(in_18), .in_2(in_19), .in_3(in_20), .in_9(in_9), .out_10(memory_8_bit_3_out_10),
    .out_11(memory_8_bit_3_out_11), .out_12(memory_8_bit_3_out_12));  // open: in_4, in_5, in_6, in_7, in_8, out_13, out_14, out_15, out_16, out_17, out_18
  ULA ula_1 (
    .in_1(memory_8_bit_1_out_10), .in_2(memory_8_bit_1_out_11), .in_3(memory_8_bit_1_out_12),
    .in_4(memory_8_bit_1_out_13), .in_5(memory_8_bit_1_out_14), .in_6(memory_8_bit_1_out_15),
    .in_7(memory_8_bit_1_out_16), .in_8(memory_8_bit_1_out_17), .in_9(memory_8_bit_2_out_10),
    .in_10(memory_8_bit_2_out_11), .in_11(memory_8_bit_2_out_12), .in_12(memory_8_bit_2_out_13),
    .in_13(memory_8_bit_2_out_14), .in_14(memory_8_bit_2_out_15), .in_15(memory_8_bit_2_out_16),
    .in_16(memory_8_bit_2_out_17), .in_17(memory_8_bit_3_out_10), .in_18(memory_8_bit_3_out_11),
    .in_19(memory_8_bit_3_out_12), .out_20(out_21), .out_21(out_22), .out_22(out_23), .out_23(out_24),
    .out_24(out_25), .out_25(out_26), .out_26(out_27), .out_27(out_28), .OVERFLOW(out_29));
endmodule

module MEMORY (
  input  REST,
  input  SET,
  output out_3,
  output out_4
);

  nor nor_1 (out_3, REST, out_4);
  nor nor_2 (out_4, out_3, SET);
endmodule

module MEMORY_8_bit (
  input  in_1,
  input  in_2,
  input  in_3,
  input  in_4,
  input  in_5,
  input  in_6,
  input  in_7,
  input  in_8,
  input  in_9,
  output out_10,
  output out_11,
  output out_12,
  output out_13,
  output out_14,
  output out_15,
  output out_16,
  output out_17,
  output out_18
);

  wire memory_1_out_3, memory_2_out_3, memory_3_out_3, memory_4_out_3, memory_5_out_3, memory_6_out_3,
       memory_7_out_3, memory_8_out_3, or_1_out, or_2_out;

  MEMORY memory_1 (.REST(in_1), .SET(in_9), .out_3(memory_1_out_3), .out_4(out_10));
  MEMORY memory_2 (.REST(in_2), .SET(in_9), .out_3(memory_2_out_3), .out_4(out_11));
  MEMORY memory_3 (.REST(in_3), .SET(in_9), .out_3(memory_3_out_3), .out_4(out_12));
  MEMORY memory_4 (.REST(in_4), .SET(in_9), .out_3(memory_4_out_3), .out_4(out_13));
  MEMORY memory_5 (.REST(in_5), .SET(in_9), .out_3(memory_5_out_3), .out_4(out_14));
  MEMORY memory_6 (.REST(in_6), .SET(in_9), .out_3(memory_6_out_3), .out_4(out_15));
  MEMORY memory_7 (.REST(in_7), .SET(in_9), .out_3(memory_7_out_3), .out_4(out_16));
  MEMORY memory_8 (.REST(in_8), .SET(in_9), .out_3(memory_8_out_3), .out_4(out_17));
  or or_1 (or_1_out, memory_1_out_3, memory_2_out_3, memory_3_out_3, memory_4_out_3, memory_5_out_3);
  or or_2 (or_2_out, memory_6_out_3, memory_7_out_3, memory_8_out_3);
  or or_3 (out_18, or_1_out, or_2_out);
endmodule
